// Logisim project alu.circ as structural Verilog: 1 circuit, main circuit main
module main (
  input  A0,
  input  A1,
  input  A2,
  input  A3,
  input  B0,
  input  B1,
  input  B2,
  input  CLOCK,
  input  B3,
  input  in_10,
  input  S1,
  input  S2,
  input  in_13,
  output out_14,
  output out_15,
  output out_16,
  output out_17
);

  wire multiplexer_2_out, multiplexer_3_out, multiplexer_4_out, multiplexer_5_out;
  wire [3:0] main_1_p9, main_2_p9, main_3_p9, main_4_p9, main_5_p9, main_6_p9, multiplexer_1_out;

  // add_main main_1: pin names not known; wires that end beside it: A0, A1, A2, A3, B0, B1, B2, B3, main_1_p9[0], main_1_p9[1], main_1_p9[2], main_1_p9[3]
  // or_main main_2: pin names not known; wires that end beside it: A0, A1, A2, A3, B0, B1, B2, B3, main_2_p9[0], main_2_p9[1], main_2_p9[2], main_2_p9[3]
  // and_main main_3: pin names not known; wires that end beside it: A0, A1, A2, A3, B0, B1, B2, B3, main_3_p9[0], main_3_p9[1], main_3_p9[2], main_3_p9[3]
  // xor_main main_4: pin names not known; wires that end beside it: A0, A1, A2, A3, B0, B1, B2, B3, main_4_p9[0], main_4_p9[1], main_4_p9[2], main_4_p9[3]
  // sub_main main_5: pin names not known; wires that end beside it: A0, A1, A2, A3, B0, B1, B2, B3, main_5_p9[0], main_5_p9[1], main_5_p9[2], main_5_p9[3]
  // not_main main_6: pin names not known; wires that end beside it: A0, A1, A2, A3, B0, B1, B2, B3, main_6_p9[0], main_6_p9[1], main_6_p9[2], main_6_p9[3]
  Multiplexer #(.select(3), .width(4)) multiplexer_1 (
    .in0(main_1_p9), .in1(main_2_p9), .in2(main_3_p9), .in3(main_4_p9), .in4(main_5_p9), .in5(main_6_p9),
    .out(multiplexer_1_out), .sel({in_13, S2, S1}));  // open: in6, in7, en
  Multiplexer multiplexer_2 (
    .in0(out_14), .in1(multiplexer_1_out[0]), .out(multiplexer_2_out), .sel(in_10));  // open: en
  Multiplexer multiplexer_3 (
    .in0(out_15), .in1(multiplexer_1_out[1]), .out(multiplexer_3_out), .sel(in_10));  // open: en
  Multiplexer multiplexer_4 (
    .in0(out_16), .in1(multiplexer_1_out[2]), .out(multiplexer_4_out), .sel(in_10));  // open: en
  Multiplexer multiplexer_5 (
    .in0(out_17), .in1(multiplexer_1_out[3]), .out(multiplexer_5_out), .sel(in_10));  // open: en
  D_Flip_Flop d_ff_1 (.clk(CLOCK), .D(multiplexer_2_out), .Q(out_14));  // open: Qn, preset, en, reset
  D_Flip_Flop d_ff_2 (.clk(CLOCK), .D(multiplexer_3_out), .Q(out_15));  // open: Qn, preset, en, reset
  D_Flip_Flop d_ff_3 (.clk(CLOCK), .D(multiplexer_4_out), .Q(out_16));  // open: Qn, preset, en, reset
  D_Flip_Flop d_ff_4 (.clk(CLOCK), .D(multiplexer_5_out), .Q(out_17));  // open: Qn, preset, en, reset

  // Notes on the sheet:
  //   ADD
  //   OR
  //   AND
  //   XOR
  //   SUB
  //   not
  //   S0
  //   ENABLE
  //   4 BIT REG
endmodule
