// Logisim project main.circ as structural Verilog: 1 circuit, main circuit Display Write Enable
module Display_Write_Enable (
  input  in_1
);

  wire clock_1_out, main_1_out_11;
  wire [3:0] main_2_out_14, multiplexer_1_out, rom_1_data, rom_1_data_2;
  wire [6:0] main_1_out_12;
  wire [7:0] counter_1_q, rom_2_data;

  Counter counter_1 (.Q(counter_1_q), .clk(clock_1_out), .clr(in_1));  // open: load, D, count, carry
  Clock clock_1 (.out(clock_1_out));
  ROM rom_1 (.addr(counter_1_q), .data({rom_1_data, rom_1_data_2}));  // open: sel
  ROM #(.addrWidth(4)) rom_2 (.addr(rom_1_data), .data(rom_2_data));  // open: sel
  Multiplexer #(.width(4)) multiplexer_1 (
    .in0(rom_1_data_2), .in1(main_2_out_14), .out(multiplexer_1_out), .sel(rom_2_data[3]));  // open: en
  registers_file_main main_1 (
    ._0(multiplexer_1_out[0]), ._1(multiplexer_1_out[1]), ._2(multiplexer_1_out[2]),
    ._3(multiplexer_1_out[3]), .Write_Enable(rom_2_data[0]), .Select(rom_2_data[1]), .in_1(clock_1_out),
    .out_8(main_1_out_12[4]), .out_9(main_1_out_12[5]), .out_10(main_1_out_12[6]), .out_11(main_1_out_11),
    .out_12(main_1_out_12[0]), .out_13(main_1_out_12[1]), .out_14(main_1_out_12[2]), .out_15(main_1_out_12[3]));
  alu_main main_2 (
    .A0(main_1_out_12[4]), .A1(main_1_out_12[5]), .A2(main_1_out_12[6]), .A3(main_1_out_11),
    .B0(main_1_out_12[0]), .B1(main_1_out_12[1]), .B2(main_1_out_12[2]), .B3(main_1_out_12[3]),
    .CLOCK(clock_1_out), .S1(rom_2_data[5]), .S2(rom_2_data[6]), .in_13(rom_2_data[7]),
    .in_10(rom_2_data[4]), .out_14(main_2_out_14[0]), .out_15(main_2_out_14[1]), .out_16(main_2_out_14[2]),
    .out_17(main_2_out_14[3]));
  TTY tty_1 (.data(main_1_out_12), .clk(clock_1_out), .we(rom_2_data[2]), .clr(in_1));

  // Notes on the sheet:
  //   A
  //   contents of rom_1 (hex, n*v repeats v):
  //   14 23 30 14 21 30 12 20 30 14 21 30 17 23 30 17 23 30 16 29 30 16 27 30 16 2e 30 16 2d 30 16 25 30
  //   16 2e 30 17 24 30 12 20 30 16 26 30 17 22 30 16 2f 30 16 2d 30 12 20 30 14 21 30 16 21 30 17 29 30
  //   17 25 30 17 23 30 16 28 30 12 2e 30 10 20 30 10 2a 30 13 24 30 12 2b 30 13 23 30 13 2d 30 14 23 50
  //   13 40 30 10 2a 30 13 25 30 12 2d 30 13 23 30 13 2d 30 15 23 60 13 40 30 10 2a 30 13 25 30 12 26 30
  //   13 26 30 13 2d 30 15 26 70 40 13 30 10 2a 30 13 25 30 17 2c 30 13 26 30 13 2d 30 15 26 80 40 13 30
  //   10 2a 30 13 25 30 15 2e 30 13 26 30 13 2d 30 15 26 90 40 13 30 10 2a 30 12 21 30 13 29 30 13 2d 30
  //   19 20 a0 40 13 30 10 2a 30
  //   Control Logic of register_file & ALU
  //   B
  //   contents of rom_2 (hex, n*v repeats v):
  //   0 1 3 4 b 10 90 50 30 70 b0
  //   REGISTER FILE
  //   Display Wirte Enable
  //   ALU
endmodule
