// Logisim project registers_file.circ as structural Verilog: 1 circuit, main circuit main
module main (
  input  in_1,
  input  _0,
  input  _1,
  input  _2,
  input  _3,
  input  Write_Enable,
  input  Select,
  output out_8,
  output out_9,
  output out_10,
  output out_11,
  output out_12,
  output out_13,
  output out_14,
  output out_15
);

  wire and_1_out, and_2_out, multiplexer_1_out, multiplexer_2_out, multiplexer_3_out, multiplexer_4_out,
       multiplexer_5_out, multiplexer_6_out, multiplexer_7_out, multiplexer_8_out, not_1_out;

  not not_1 (not_1_out, Select);
  and and_1 (and_1_out, Write_Enable, Select);
  and and_2 (and_2_out, Write_Enable, not_1_out);
  Multiplexer multiplexer_1 (.in0(out_8), .in1(_0), .out(multiplexer_1_out), .sel(and_2_out));  // open: en
  Multiplexer multiplexer_2 (.in0(out_9), .in1(_1), .out(multiplexer_2_out), .sel(and_2_out));  // open: en
  Multiplexer multiplexer_3 (.in0(out_10), .in1(_2), .out(multiplexer_3_out), .sel(and_2_out));  // open: en
  Multiplexer multiplexer_4 (.in0(out_11), .in1(_3), .out(multiplexer_4_out), .sel(and_2_out));  // open: en
  Multiplexer multiplexer_5 (.in0(out_12), .in1(_0), .out(multiplexer_5_out), .sel(and_1_out));  // open: en
  Multiplexer multiplexer_6 (.in0(out_13), .in1(_1), .out(multiplexer_6_out), .sel(and_1_out));  // open: en
  Multiplexer multiplexer_7 (.in0(out_14), .in1(_2), .out(multiplexer_7_out), .sel(and_1_out));  // open: en
  Multiplexer multiplexer_8 (.in0(out_15), .in1(_3), .out(multiplexer_8_out), .sel(and_1_out));  // open: en
  D_Flip_Flop d_ff_1 (.clk(in_1), .D(multiplexer_1_out), .Q(out_8));  // open: Qn, preset, en, reset
  D_Flip_Flop d_ff_2 (.clk(in_1), .D(multiplexer_2_out), .Q(out_9));  // open: Qn, preset, en, reset
  D_Flip_Flop d_ff_3 (.clk(in_1), .D(multiplexer_3_out), .Q(out_10));  // open: Qn, preset, en, reset
  D_Flip_Flop d_ff_4 (.clk(in_1), .D(multiplexer_4_out), .Q(out_11));  // open: Qn, preset, en, reset
  D_Flip_Flop d_ff_5 (.clk(in_1), .D(multiplexer_5_out), .Q(out_12));  // open: Qn, preset, en, reset
  D_Flip_Flop d_ff_6 (.clk(in_1), .D(multiplexer_6_out), .Q(out_13));  // open: Qn, preset, en, reset
  D_Flip_Flop d_ff_7 (.clk(in_1), .D(multiplexer_7_out), .Q(out_14));  // open: Qn, preset, en, reset
  D_Flip_Flop d_ff_8 (.clk(in_1), .D(multiplexer_8_out), .Q(out_15));  // open: Qn, preset, en, reset
endmodule
